// Logisim project k-map circuit-logism.circ as structural Verilog: 1 circuit, main circuit main
module main (
  input  I0,
  input  I1,
  input  I2,
  input  I3,
  output out_5,
  output out_6,
  output out_7,
  output out_8
);

  wire and_1_out, and_2_out, and_3_out, and_4_out, and_5_out, and_6_out, and_7_out, and_8_out, and_9_out,
       and_10_out, and_11_out, and_12_out, and_13_out, and_14_out, and_15_out, and_16_out, and_17_out,
       not_1_out, not_2_out, not_3_out, not_4_out;

  not not_1 (not_1_out, I0);
  not not_2 (not_2_out, I1);
  not not_3 (not_3_out, I2);
  not not_4 (not_4_out, I3);
  and and_1 (and_1_out, not_1_out, not_2_out, not_3_out, I3);
  and and_2 (and_2_out, not_1_out, not_2_out, I2, not_4_out);
  and and_3 (and_3_out, I0, I1, I2, not_4_out);
  and and_4 (and_4_out, I0, not_2_out, I2, I3);
  and and_5 (and_5_out, I0, not_2_out, I2, I3);
  and and_6 (and_6_out, not_1_out, not_2_out, not_3_out);
  and and_7 (and_7_out, not_1_out, I1, I2);
  and and_8 (and_8_out, not_1_out, not_4_out);
  and and_9 (and_9_out, not_2_out, not_4_out);
  and and_10 (and_10_out, not_1_out, I1, not_3_out);
  and and_11 (and_11_out, I1, not_3_out, I3);
  and and_12 (and_12_out, I0, I2);
  and and_13 (and_13_out, I2, not_4_out);
  and and_14 (and_14_out, not_1_out, not_3_out, not_4_out);
  and and_15 (and_15_out, I0, I1, I3);
  and and_16 (and_16_out, not_2_out, I2, I3);
  and and_17 (and_17_out, I0, I1, I2);
  or or_1 (out_5, and_1_out, and_2_out, and_3_out, and_4_out, and_5_out);
  or or_2 (out_6, and_6_out, and_7_out, and_8_out, and_9_out);
  or or_3 (out_7, and_10_out, and_11_out, and_12_out, and_13_out);
  or or_4 (out_8, and_14_out, and_15_out, and_16_out, and_17_out);
endmodule
